# Fritzing sketch Tp2 Joystick (saved by Fritzing 0.9.10b)

parts:
  part = Thumb Joystick
  Mod1 = Raspberry Pi Pico
  R1 = Resistor [tolerance=±5% power=0.25 resistance=220 package=THT]
  LED1 = smd LED [color="Red (633nm)" package="1206 [SMD]"]

nets:
  N1: part.GND, Mod1.pin_8, Mod1.pin_33
  N2: part.SEL, Mod1.pin_5
  N3: part.HORZ, Mod1.pin_32
  N4: part.VERT, Mod1.pin_31
  N5: part.VCC, Mod1.pin_40
  N6: Mod1.pin_1, LED1.anode
  N7: Mod1.pin_4, R1.Pin_1
  N8: R1.Pin_0, LED1.cathode

custom parts:
  Raspberry Pi Pico: Raspberry Pi Pico. Based around the RP2040 microcontroller the Pico is a low cost microcontroller device bringing Raspberry Pi quality, cost, and easy of use to the microcontroller space. Jan 2021, Split part in to two versions: tht (this one) and SMD. This one will drill holes for a .1 in header in pcb to allow plugging in the module as well as providing pads to solder the module to the top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
