# Fritzing sketch Tp 4 cablage joystick moteur l298n (saved by Fritzing 0.9.10b)

parts:
  Mod1 = Raspberry Pi Pico
  L298N2 = L298N DC motor driver
  Composant1 = Thumb Joystick
  M2 = DC Motor [voltage_(max)=6V voltage_(min)=3V]

nets:
  N1: Mod1.pin_1, L298N2.ENA
  N2: Mod1.pin_2, L298N2.IN1
  N3: Mod1.pin_4, L298N2.IN2
  N4: Mod1.pin_5, Composant1.SEL
  N5: Mod1.pin_31, Composant1.VERT
  N6: Mod1.pin_32, Composant1.HORZ
  N7: Mod1.pin_33, Composant1.GND
  5V: Mod1.pin_40, L298N2.5V, Composant1.VCC
  N8: L298N2.OUT1, M2.pin_2
  N9: L298N2.OUT2, M2.pin_1

custom parts:
  Raspberry Pi Pico: Raspberry Pi Pico. Based around the RP2040 microcontroller the Pico is a low cost microcontroller device bringing Raspberry Pi quality, cost, and easy of use to the microcontroller space. Jan 2021, Split part in to two versions: tht (this one) and SMD. This one will drill holes for a .1 in header in pcb to allow plugging in the module as well as providing pads to solder the module to the top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
  L298N DC motor driver: 2x DC motor driver with 78M05 positive voltage regulator (7..35 V) L298N: max 46 V, 2 A Set 5 V Enable jumper to enable 5 V regultor (needed for the L298N) and +5 V output at screw terminal or supply external +5 V at screw terminal Set ENA and/or ENB to +5 V to enable motor permanently or supply ENA and/or ENB with PWM signal IN1 and IN2 set rotation directory for motor A (OUT1/OUT2) IN2 and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
