# Fritzing sketch Tp 5 Bluetooth (saved by Fritzing 0.9.10b)

parts:
  Mod2 = Raspberry Pi Pico
  Composant2 = Bluetooth HC-05 Macho
  Mod3 = Raspberry Pi Pico
  Composant3 = Bluetooth HC-05 Macho

nets:
  N1: Mod2.pin_1, Composant2.TXD
  N2: Mod2.pin_2, Composant2.RXD
  N3: Mod2.pin_38, Composant2.GND
  N4: Mod2.pin_40, Composant2.VCC
  N5: Mod3.pin_1, Composant3.TXD
  N6: Mod3.pin_2, Composant3.RXD
  N7: Mod3.pin_38, Mod3.pin_42, Composant3.GND
  N8: Mod3.pin_40, Composant3.VCC

custom parts:
  Raspberry Pi Pico: Raspberry Pi Pico. Based around the RP2040 microcontroller the Pico is a low cost microcontroller device bringing Raspberry Pi quality, cost, and easy of use to the microcontroller space. Jan 2021, Split part in to two versions: tht (this one) and SMD. This one will drill holes for a .1 in header in pcb to allow plugging in the module as well as providing pads to solder the module to the top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
